// Logisim project 实验1_1.circ as structural Verilog: 5 circuits, main circuit main
module main (
  input  C0,
  input  A3,
  input  A2,
  input  A1,
  input  A0,
  input  B3,
  input  B2,
  input  B1,
  input  B0,
  output S3,
  output S2,
  output S1,
  output S0,
  output C4
);

  \先行进位的四位二进制并行加法器  \u_先行进位的四位二进制并行加法器_1  (
    .A3(A3), .B3(B3), .A2(A2), .B2(B2), .A1(A1), .B1(B1), .A0(A0), .B0(B0), .C0(C0), .C4(C4), .S3(S3),
    .S2(S2), .S1(S1), .S0(S0));
endmodule

module \一位二进制半加器  (
  input  A,
  input  B,
  output C,
  output S
);

  and and_1 (C, B, A);
  xor xor_1 (S, B, A);

  // Notes on the sheet:
  //   一位二进制半加器
endmodule

module \一位二进制全加器  (
  input  A,
  input  B,
  input  Ci,
  output S,
  output Co
);

  wire and_1_out, and_2_out, xor_2_out;

  xor xor_1 (S, xor_2_out, Ci);
  xor xor_2 (xor_2_out, A, B);
  and and_1 (and_1_out, xor_2_out, Ci);
  or or_1 (Co, and_1_out, and_2_out);
  and and_2 (and_2_out, A, B);

  // Notes on the sheet:
  //   一位二进制全加器
endmodule

module \串行进位的四位二进制并行加法器  (
  input  C0,
  input  A3,
  input  B3,
  input  A2,
  input  B2,
  input  A1,
  input  B1,
  input  A0,
  input  B0,
  output S3,
  output S2,
  output S1,
  output S0,
  output C4
);

  wire \一位二进制全加器_2_co , \一位二进制全加器_3_co , \一位二进制全加器_4_co ;

  \一位二进制全加器  \u_一位二进制全加器_1  (.S(S3), .Co(C4), .A(A3), .B(B3), .Ci(\一位二进制全加器_2_co ));
  \一位二进制全加器  \u_一位二进制全加器_2  (.S(S2), .Co(\一位二进制全加器_2_co ), .A(A2), .B(B2), .Ci(\一位二进制全加器_3_co ));
  \一位二进制全加器  \u_一位二进制全加器_3  (.S(S1), .Co(\一位二进制全加器_3_co ), .A(A1), .B(B1), .Ci(\一位二进制全加器_4_co ));
  \一位二进制全加器  \u_一位二进制全加器_4  (.S(S0), .Co(\一位二进制全加器_4_co ), .A(A0), .B(B0), .Ci(C0));
endmodule

module \先行进位的四位二进制并行加法器  (
  input  C0,
  input  A3,
  input  B3,
  input  A2,
  input  B2,
  input  A1,
  input  B1,
  input  A0,
  input  B0,
  output S3,
  output S2,
  output S1,
  output S0,
  output C4
);

  wire and_1_out, and_2_out, and_3_out, and_4_out, and_5_out, and_6_out, and_7_out, and_8_out, and_9_out,
       and_10_out, C1_out, C2_out, C3_out, G1_out, G2_out, G3_out, G4_out, P1_out, P2_out, P3_out, P4_out;

  xor u_S3 (S3, P4_out, C3_out);
  xor u_S2 (S2, P3_out, C2_out);
  and G4 (G4_out, A3, B3);
  xor u_S1 (S1, P2_out, C1_out);
  and G3 (G3_out, A2, B2);
  xor u_S0 (S0, P1_out, C0);
  and G2 (G2_out, A1, B1);
  and and_1 (and_1_out, G3_out, P4_out);
  and G1 (G1_out, A0, B0);
  or u_C4 (C4, and_1_out, and_2_out, G4_out, and_3_out, and_4_out);
  and and_2 (and_2_out, G2_out, P4_out, P3_out);
  and and_3 (and_3_out, G1_out, P4_out, P3_out, P2_out);
  xor P4 (P4_out, A3, B3);
  and and_4 (and_4_out, P4_out, P3_out, P2_out, P1_out, C0);
  and and_5 (and_5_out, G2_out, P3_out);
  or C3 (C3_out, G3_out, and_5_out, and_6_out, and_7_out);
  and and_6 (and_6_out, G1_out, P3_out, P2_out);
  xor P3 (P3_out, A2, B2);
  and and_7 (and_7_out, P3_out, P2_out, P1_out, C0);
  or C2 (C2_out, and_8_out, G2_out, and_9_out);
  and and_8 (and_8_out, G1_out, P2_out);
  and and_9 (and_9_out, P2_out, P1_out, C0);
  xor P2 (P2_out, A1, B1);
  or C1 (C1_out, G1_out, and_10_out);
  and and_10 (and_10_out, P1_out, C0);
  xor P1 (P1_out, A0, B0);
endmodule
