// Logisim project 实验1_2.circ as structural Verilog
module \四位二进制可逆计数器  (
  input  \置0 ,
  input  CPU,
  input  CPD,
  output Q3,
  output Q2,
  output Q1,
  output Q0
);

  wire and_1_out, and_2_out, and_3_out, and_4_out, and_5_out, and_6_out, D0_qn, D1_qn, D2_qn, D3_qn,
       or_1_out, or_2_out, or_3_out, or_4_out;

  and and_1 (and_1_out, CPD, D1_qn, D0_qn, D2_qn);
  D_Flip_Flop #(.trigger("falling")) D3 (
    .clk(or_1_out), .D(D3_qn), .Q(Q3), .Qn(D3_qn), .en(1'b1), .reset(\置0 ));  // open: preset
  or or_1 (or_1_out, and_1_out, and_2_out);
  and and_2 (and_2_out, CPU, Q1, Q0, Q2);
  or or_2 (or_2_out, and_3_out, and_4_out);
  and and_3 (and_3_out, CPD, D0_qn, D1_qn);
  D_Flip_Flop #(.trigger("falling")) D2 (
    .clk(or_2_out), .D(D2_qn), .Q(Q2), .Qn(D2_qn), .en(1'b1), .reset(\置0 ));  // open: preset
  and and_4 (and_4_out, CPU, Q0, Q1);
  and and_5 (and_5_out, CPD, D0_qn);
  D_Flip_Flop #(.trigger("falling")) D1 (
    .clk(or_3_out), .D(D1_qn), .Q(Q1), .Qn(D1_qn), .en(1'b1), .reset(\置0 ));  // open: preset
  or or_3 (or_3_out, and_5_out, and_6_out);
  and and_6 (and_6_out, CPU, Q0);
  or or_4 (or_4_out, CPD, CPU);
  D_Flip_Flop #(.trigger("falling")) D0 (
    .clk(or_4_out), .D(D0_qn), .Q(Q0), .Qn(D0_qn), .en(1'b1), .reset(\置0 ));  // open: preset

  // Notes on the sheet:
  //   四位二进制可逆计数器
endmodule

module \四位二进制可逆计数器验证  (
  input  in_1,
  input  in_2,
  input  in_3,
  output out_4,
  output out_5,
  output out_6,
  output out_7
);

  \四位二进制可逆计数器  \u_四位二进制可逆计数器_1  (.Q3(out_4), .Q2(out_5), .Q1(out_6), .Q0(out_7), .\置0 (in_2), .CPU(in_1), .CPD(in_3));
endmodule

module \_4位二进制数转8421码  (
  input  A3,
  input  A2,
  input  A1,
  input  A0,
  output S80,
  output S40,
  output S20,
  output S10,
  output S8,
  output S4,
  output S2,
  output S1
);

  wire and_1_out, or_1_out;

  \先行进位的四位二进制并行加法器  \u_先行进位的四位二进制并行加法器_1  (
    .A3(A3), .B3(1'b0), .A2(A2), .B2(and_1_out), .A1(A1), .B1(and_1_out), .A0(A0), .B0(1'b0), .C0(1'b0),
    .C4(S10), .S3(S8), .S2(S4), .S1(S2), .S0(S1));
  and and_1 (and_1_out, A3, or_1_out);
  or or_1 (or_1_out, A1, A2);

  assign S20 = 1'b0;
  assign S40 = 1'b0;
  assign S80 = 1'b0;

  // Notes on the sheet:
  //   4位二进制数转8421码
  //   十位
  //   个位
endmodule

module \四位二进制数转8421码验证  (
  input  A4,
  input  A3,
  input  A2,
  input  A1,
  output \十位 ,
  output out_6,
  output out_7,
  output out_8,
  output out_9,
  output \个位 ,
  output out_11,
  output out_12
);

  \_4位二进制数转8421码  \u_4位二进制数转8421码_1  (
    .S80(\十位 ), .S40(out_6), .S20(out_7), .S10(out_8), .S8(out_9), .S4(\个位 ), .S2(out_11), .S1(out_12),
    .A3(A4), .A2(A3), .A1(A2), .A0(A1));
endmodule

module \_7段译码器  (
  input  A3,
  input  A2,
  input  A1,
  input  A0,
  output a,
  output b,
  output c,
  output d,
  output e,
  output f,
  output g
);

  wire and_1_out, and_2_out, and_3_out, and_4_out, and_5_out, and_6_out, and_7_out, and_8_out, and_9_out,
       and_10_out, and_11_out, and_12_out, and_13_out, and_14_out, and_15_out, and_16_out, and_17_out,
       and_18_out, and_19_out, and_20_out, and_21_out, not_1_out, not_2_out, not_3_out, not_4_out;

  not not_1 (not_1_out, A3);
  not not_2 (not_2_out, A2);
  not not_3 (not_3_out, A1);
  not not_4 (not_4_out, A0);
  and and_1 (and_1_out, not_2_out, not_3_out, not_4_out);
  and and_2 (and_2_out, not_1_out, not_2_out, A1);
  and and_3 (and_3_out, not_1_out, A2, A0);
  and and_4 (and_4_out, A3, not_3_out, A0);
  and and_5 (and_5_out, not_1_out, A1, A0);
  and and_6 (and_6_out, not_1_out, not_2_out);
  and and_7 (and_7_out, not_3_out, not_4_out);
  and and_8 (and_8_out, not_2_out, not_3_out);
  and and_9 (and_9_out, not_1_out, A2);
  and and_10 (and_10_out, not_2_out, A0);
  and and_11 (and_11_out, not_2_out, not_4_out);
  and and_12 (and_12_out, A2, not_3_out, A0);
  and and_13 (and_13_out, not_2_out, A1, A0);
  and and_14 (and_14_out, A2, A1, not_4_out);
  and and_15 (and_15_out, A1, not_4_out);
  and and_16 (and_16_out, not_3_out, not_4_out);
  and and_17 (and_17_out, A2, not_3_out);
  and and_18 (and_18_out, A2, not_4_out);
  and and_19 (and_19_out, A3, not_2_out, not_3_out);
  and and_20 (and_20_out, A3, not_2_out);
  and and_21 (and_21_out, not_2_out, A1);
  or or_1 (a, and_1_out, and_2_out, and_3_out, and_4_out);
  or or_2 (b, and_5_out, and_6_out, and_7_out, and_8_out);
  or or_3 (c, and_8_out, and_9_out, and_10_out);
  or or_4 (d, and_11_out, and_12_out, and_13_out, and_14_out);
  or or_5 (e, and_11_out, and_15_out);
  or or_6 (f, and_16_out, and_17_out, and_18_out, and_19_out);
  or or_7 (g, and_15_out, and_17_out, and_20_out, and_21_out);

  // Notes on the sheet:
  //   7段译码器
endmodule

module \_7段译码器显示人数电路  (
  input  in_1,
  input  in_2,
  input  in_3,
  input  in_4
);

  wire \n4位二进制数转8421码_1_s1 , \n4位二进制数转8421码_1_s2 , \n4位二进制数转8421码_1_s4 , \n4位二进制数转8421码_1_s8 ,
       \n4位二进制数转8421码_1_s10 , \n4位二进制数转8421码_1_s20 , \n4位二进制数转8421码_1_s40 , \n4位二进制数转8421码_1_s80 ,
       \n7段译码器_1_a , \n7段译码器_1_b , \n7段译码器_1_c , \n7段译码器_1_d , \n7段译码器_1_e , \n7段译码器_1_f , \n7段译码器_1_g ,
       \n7段译码器_2_a , \n7段译码器_2_b , \n7段译码器_2_c , \n7段译码器_2_d , \n7段译码器_2_e , \n7段译码器_2_f , \n7段译码器_2_g ;

  _7_Segment_Display u_7_segment_display_1 (
    .g(\n7段译码器_1_g ), .f(\n7段译码器_1_f ), .a(\n7段译码器_1_a ), .b(\n7段译码器_1_b ), .e(\n7段译码器_1_e ),
    .d(\n7段译码器_1_d ), .c(\n7段译码器_1_c ));  // open: dp
  \_7段译码器  \u_7段译码器_1  (
    .A3(\n4位二进制数转8421码_1_s80 ), .A2(\n4位二进制数转8421码_1_s40 ), .A1(\n4位二进制数转8421码_1_s20 ),
    .A0(\n4位二进制数转8421码_1_s10 ), .a(\n7段译码器_1_a ), .b(\n7段译码器_1_b ), .c(\n7段译码器_1_c ), .d(\n7段译码器_1_d ),
    .e(\n7段译码器_1_e ), .f(\n7段译码器_1_f ), .g(\n7段译码器_1_g ));
  \_4位二进制数转8421码  \u_4位二进制数转8421码_1  (
    .S80(\n4位二进制数转8421码_1_s80 ), .S40(\n4位二进制数转8421码_1_s40 ), .S20(\n4位二进制数转8421码_1_s20 ),
    .S10(\n4位二进制数转8421码_1_s10 ), .S8(\n4位二进制数转8421码_1_s8 ), .S4(\n4位二进制数转8421码_1_s4 ),
    .S2(\n4位二进制数转8421码_1_s2 ), .S1(\n4位二进制数转8421码_1_s1 ), .A3(in_1), .A2(in_2), .A1(in_3), .A0(in_4));
  _7_Segment_Display u_7_segment_display_2 (
    .g(\n7段译码器_2_g ), .f(\n7段译码器_2_f ), .a(\n7段译码器_2_a ), .b(\n7段译码器_2_b ), .e(\n7段译码器_2_e ),
    .d(\n7段译码器_2_d ), .c(\n7段译码器_2_c ));  // open: dp
  \_7段译码器  \u_7段译码器_2  (
    .A3(\n4位二进制数转8421码_1_s8 ), .A2(\n4位二进制数转8421码_1_s4 ), .A1(\n4位二进制数转8421码_1_s2 ),
    .A0(\n4位二进制数转8421码_1_s1 ), .a(\n7段译码器_2_a ), .b(\n7段译码器_2_b ), .c(\n7段译码器_2_c ), .d(\n7段译码器_2_d ),
    .e(\n7段译码器_2_e ), .f(\n7段译码器_2_f ), .g(\n7段译码器_2_g ));
endmodule

module \门禁_不_动作  (
  input  U,
  input  CLR,
  input  D,
  output out_4,
  output out_5,
  output out_6,
  output out_7
);

  wire and_1_out, and_2_out, not_1_out, \报警信号_out , \无人信号_out , \满员信号_out ;

  LED led_1 (.in(\报警信号_out ));
  and \u_报警信号  (\报警信号_out , U, \满员信号_out );
  not not_1 (not_1_out, \满员信号_out );
  and and_1 (and_1_out, not_1_out, U);
  and and_2 (and_2_out, \无人信号_out , D);
  or \u_无人信号  (\无人信号_out , out_7, out_6, out_5, out_4);
  and \u_满员信号  (\满员信号_out , out_7, out_6, out_5, out_4);
  \四位二进制可逆计数器  \u_四位二进制可逆计数器_1  (
    .Q3(out_4), .Q2(out_5), .Q1(out_6), .Q0(out_7), .\置0 (CLR), .CPU(and_1_out), .CPD(and_2_out));

  // Notes on the sheet:
  //   报警灯
  //   实验室满员报警系统
endmodule

module \小型实验室门禁系统  (
  input  U,
  input  CLR,
  input  D,
  output a1,
  output b1,
  output c1,
  output d1,
  output e1,
  output f1,
  output g1,
  output a0,
  output b0,
  output c0,
  output d0,
  output e0,
  output f0,
  output g0,
  output Z
);

  wire and_1_out, and_2_out, \n4位二进制数转8421码_1_s1 , \n4位二进制数转8421码_1_s2 , \n4位二进制数转8421码_1_s4 ,
       \n4位二进制数转8421码_1_s8 , \n4位二进制数转8421码_1_s10 , \n4位二进制数转8421码_1_s20 , \n4位二进制数转8421码_1_s40 ,
       \n4位二进制数转8421码_1_s80 , not_1_out, \四位二进制可逆计数器_1_q0 , \四位二进制可逆计数器_1_q1 , \四位二进制可逆计数器_1_q2 ,
       \四位二进制可逆计数器_1_q3 , \无人信号_out , \满员信号_out ;

  and \u_报警信号  (Z, U, \满员信号_out );
  or \u_无人信号  (\无人信号_out , \四位二进制可逆计数器_1_q0 , \四位二进制可逆计数器_1_q1 , \四位二进制可逆计数器_1_q2 , \四位二进制可逆计数器_1_q3 );
  not not_1 (not_1_out, \满员信号_out );
  and \u_满员信号  (\满员信号_out , \四位二进制可逆计数器_1_q0 , \四位二进制可逆计数器_1_q1 , \四位二进制可逆计数器_1_q2 , \四位二进制可逆计数器_1_q3 );
  and and_1 (and_1_out, not_1_out, U);
  and and_2 (and_2_out, \无人信号_out , D);
  \_7段译码器  \u_7段译码器_1  (
    .A3(\n4位二进制数转8421码_1_s80 ), .A2(\n4位二进制数转8421码_1_s40 ), .A1(\n4位二进制数转8421码_1_s20 ),
    .A0(\n4位二进制数转8421码_1_s10 ), .a(a1), .b(b1), .c(c1), .d(d1), .e(e1), .f(f1), .g(g1));
  \_4位二进制数转8421码  \u_4位二进制数转8421码_1  (
    .S80(\n4位二进制数转8421码_1_s80 ), .S40(\n4位二进制数转8421码_1_s40 ), .S20(\n4位二进制数转8421码_1_s20 ),
    .S10(\n4位二进制数转8421码_1_s10 ), .S8(\n4位二进制数转8421码_1_s8 ), .S4(\n4位二进制数转8421码_1_s4 ),
    .S2(\n4位二进制数转8421码_1_s2 ), .S1(\n4位二进制数转8421码_1_s1 ), .A3(\四位二进制可逆计数器_1_q3 ), .A2(\四位二进制可逆计数器_1_q2 ),
    .A1(\四位二进制可逆计数器_1_q1 ), .A0(\四位二进制可逆计数器_1_q0 ));
  \四位二进制可逆计数器  \u_四位二进制可逆计数器_1  (
    .Q3(\四位二进制可逆计数器_1_q3 ), .Q2(\四位二进制可逆计数器_1_q2 ), .Q1(\四位二进制可逆计数器_1_q1 ), .Q0(\四位二进制可逆计数器_1_q0 ),
    .\置0 (CLR), .CPU(and_1_out), .CPD(and_2_out));
  \_7段译码器  \u_7段译码器_2  (
    .A3(\n4位二进制数转8421码_1_s8 ), .A2(\n4位二进制数转8421码_1_s4 ), .A1(\n4位二进制数转8421码_1_s2 ),
    .A0(\n4位二进制数转8421码_1_s1 ), .a(a0), .b(b0), .c(c0), .d(d0), .e(e0), .f(f0), .g(g0));

  // Notes on the sheet:
  //   小型实验室门禁系统
endmodule

module \小型实验室门禁系统验证  (
  input  U,
  input  CLR,
  input  D
);

  wire \小型实验室门禁系统_1_a0 , \小型实验室门禁系统_1_a1 , \小型实验室门禁系统_1_b0 , \小型实验室门禁系统_1_b1 , \小型实验室门禁系统_1_c0 ,
       \小型实验室门禁系统_1_c1 , \小型实验室门禁系统_1_d0 , \小型实验室门禁系统_1_d1 , \小型实验室门禁系统_1_e0 , \小型实验室门禁系统_1_e1 ,
       \小型实验室门禁系统_1_f0 , \小型实验室门禁系统_1_f1 , \小型实验室门禁系统_1_g0 , \小型实验室门禁系统_1_g1 , \小型实验室门禁系统_1_z ;

  _7_Segment_Display u_7_segment_display_1 (
    .g(\小型实验室门禁系统_1_g1 ), .f(\小型实验室门禁系统_1_f1 ), .a(\小型实验室门禁系统_1_a1 ), .b(\小型实验室门禁系统_1_b1 ),
    .e(\小型实验室门禁系统_1_e1 ), .d(\小型实验室门禁系统_1_d1 ), .c(\小型实验室门禁系统_1_c1 ));  // open: dp
  \小型实验室门禁系统  \u_小型实验室门禁系统_1  (
    .U(U), .CLR(CLR), .D(D), .Z(\小型实验室门禁系统_1_z ), .a1(\小型实验室门禁系统_1_a1 ), .b1(\小型实验室门禁系统_1_b1 ),
    .c1(\小型实验室门禁系统_1_c1 ), .d1(\小型实验室门禁系统_1_d1 ), .e1(\小型实验室门禁系统_1_e1 ), .f1(\小型实验室门禁系统_1_f1 ),
    .g1(\小型实验室门禁系统_1_g1 ), .a0(\小型实验室门禁系统_1_a0 ), .b0(\小型实验室门禁系统_1_b0 ), .c0(\小型实验室门禁系统_1_c0 ),
    .d0(\小型实验室门禁系统_1_d0 ), .e0(\小型实验室门禁系统_1_e0 ), .f0(\小型实验室门禁系统_1_f0 ), .g0(\小型实验室门禁系统_1_g0 ));
  _7_Segment_Display u_7_segment_display_2 (
    .g(\小型实验室门禁系统_1_g0 ), .f(\小型实验室门禁系统_1_f0 ), .a(\小型实验室门禁系统_1_a0 ), .b(\小型实验室门禁系统_1_b0 ),
    .e(\小型实验室门禁系统_1_e0 ), .d(\小型实验室门禁系统_1_d0 ), .c(\小型实验室门禁系统_1_c0 ));  // open: dp
  LED led_1 (.in(\小型实验室门禁系统_1_z ));
endmodule
